# Fritzing sketch circuits (saved by Fritzing 0.9.3b)
breadboards: 1

parts:
  Q1 = NPN-Transistor [package="TO92 [THT]"]  # not connected
  R1 = Resistor [tolerance=±5% resistance=1k package=THT]  # not connected
  LED1 = LED - 5mm [color="Infrared (940nm)" package="5 mm [THT]"]  # not connected
  R2 = Resistor [tolerance=±5% resistance=100 package=THT]  # not connected
  Q2 = NPN-Transistor [package="TO92 [THT]"]  # not connected
  LED2 = LED - 5mm [color="Infrared (940nm)" package="5 mm [THT]"]  # not connected
  R4 = Resistor [tolerance=±5% resistance=47 package=THT]  # not connected
  Q3 = NPN-Transistor [package="TO92 [THT]"]  # not connected
  R5 = Resistor [tolerance=±5% resistance=1k package=THT]  # not connected
  LED3 = LED - 5mm [color="Infrared (940nm)" package="5 mm [THT]"]  # not connected
  R6 = Resistor [tolerance=±5% resistance=100 package=THT]  # not connected
  Q4 = NPN-Transistor [package="TO92 [THT]"]  # not connected
  R7 = Resistor [tolerance=±5% resistance=1k package=THT]  # not connected
  Q5 = Basic FET P-Channel [package="TO220 [THT]"]
  Q6 = Basic FET P-Channel [package="TO220 [THT]"]
  LED4 = LED - 5mm [color="Infrared (940nm)" package="5 mm [THT]"]  # not connected
  R8 = Resistor [tolerance=±5% resistance=100 package=THT]  # not connected
  Q7 = NPN-Transistor [package="TO92 [THT]"]
  R9 = Resistor [tolerance=±5% resistance=1k package=THT]  # not connected
  R10 = Resistor [tolerance=±5% resistance=220 package=THT]
  J1 = female pin header, 1 pin [form="♀ (female)"]
  J1_2 = female pin header, 1 pin [form="♀ (female)"]

nets:
  N1: Q5.source, Q6.drain
  N2: Q7.C, R10.Pin_1, J1.pin1, J1_2.pin1

notes:
  To pin X1
  MPS2222A
  To pin 23
  To pin 21
  TN0702
  S
  D
  G
  Receiver o/p
  ESP32 I/P
